// Logisim project Circuitos JCC.circ as structural Verilog: 2 circuits, main circuit 1)
module main (
  input  _1,
  input  _3,
  input  _6,
  input  _2,
  input  _4,
  input  _5,
  output O
);

  wire and_1_out, and_2_out, and_3_out, and_4_out, and_5_out, and_6_out, not_1_out, not_2_out, not_3_out,
       or_1_out, or_2_out;

  and and_1 (and_1_out, _1, not_1_out);
  not not_1 (not_1_out, _2);
  and and_2 (and_2_out, _2, _3);
  and and_3 (and_3_out, _4, not_2_out);
  not not_2 (not_2_out, _2);
  and and_4 (and_4_out, _2, _5);
  or or_1 (or_1_out, and_1_out, and_2_out);
  or or_2 (or_2_out, and_3_out, and_4_out);
  and and_5 (and_5_out, or_1_out, not_3_out);
  not not_3 (not_3_out, _6);
  and and_6 (and_6_out, _6, or_2_out);
  or or_3 (O, and_5_out, and_6_out);
endmodule

module _1 (
  input  A,
  input  B,
  output O
);

  wire and_1_out, and_2_out, not_1_out, not_2_out;

  not not_1 (not_1_out, A);
  and and_1 (and_1_out, not_1_out, B);
  and and_2 (and_2_out, A, not_2_out);
  not not_2 (not_2_out, B);
  or or_1 (O, and_1_out, and_2_out);
endmodule
